// Logisim project G2.circ as structural Verilog: 2 circuits, main circuit main
module main (
);

  wire adder_1_p3, ALUSrc, Branch, MemRead, MemtoReg, MemWrite, mips_alu_1_p5, mips_alu_1_p7, RegDst,
       registerfile_1_p6, RegWrite, Tick;
  wire [1:0] ALUOp;
  wire [3:0] alu_control_1_out_2;
  wire [4:0] multiplexer_1_out;
  wire [23:0] bit_extender_2_out;
  wire [31:0] bit_extender_1_out, Control_p1, mips_alu_1_p6, mips_ram_1_p6, multiplexer_2_out, PC_q,
       registerfile_1_p1, registerfile_1_p7;

  Clock clock_1 (.out(Tick));
  Register #(.width(32)) PC (.Q(PC_q), .clk(Tick));  // open: D, en, clr
  // PLA Control: pin names not known; wires that end beside it: Control_p1[31:26]
  // Adder adder_1: pin names not known; wires that end beside it: PC_q, 32'h4, adder_1_p3, adder_1_p3, Control_p1[25:0]
  // MIPSProgramROM mipsprogramrom_1: pin names not known; wires that end beside it: PC_q, Tick, RegDst
  Multiplexer #(.width(5), .enable("false")) multiplexer_1 (
    .in0(Control_p1[20:16]), .in1(Control_p1[15:11]), .out(multiplexer_1_out), .sel(RegDst));
  // RegisterFile registerfile_1: pin names not known; wires that end beside it: registerfile_1_p1, RegWrite, multiplexer_1_out, Control_p1[25:21], Control_p1[20:16], registerfile_1_p6, registerfile_1_p7
  assign bit_extender_1_out = {{16{Control_p1[15]}}, Control_p1[15:0]};  // Bit_Extender bit_extender_1
  Multiplexer #(.width(32), .enable("false")) multiplexer_2 (
    .in0(registerfile_1_p7), .in1(bit_extender_1_out), .out(multiplexer_2_out), .sel(ALUSrc));
  ALU_control alu_control_1 (.in_1({ALUOp, Control_p1[5:0]}), .out_2(alu_control_1_out_2));
  // MIPS_ALU mips_alu_1: pin names not known; wires that end beside it: bit_extender_1_out, registerfile_1_p6, multiplexer_2_out, alu_control_1_out_2, mips_alu_1_p5, mips_alu_1_p6, mips_alu_1_p7
  Bit_Extender #(.in_width(32), .out_width(24)) bit_extender_2 (.in(mips_alu_1_p6), .out(bit_extender_2_out));
  and and_1 (mips_alu_1_p7, Branch, mips_alu_1_p5);
  // MIPS_RAM mips_ram_1: pin names not known; wires that end beside it: bit_extender_2_out, registerfile_1_p7, MemWrite, MemRead, Tick, mips_ram_1_p6
  Multiplexer #(.width(32), .enable("false")) multiplexer_3 (
    .in0(mips_alu_1_p6), .in1(mips_ram_1_p6), .out(registerfile_1_p1), .sel(MemtoReg));
endmodule

module ALU_control (
  input  [7:0] in_1,
  output [3:0] out_2
);

  // PLA ALU_Control: pin names not known; wires that end beside it: in_1, out_2
endmodule
