// Logisim project sandbox.circ as structural Verilog: 1 circuit, main circuit main
module main (
);

  wire ALUsrc, Branch, Jump, MemRead, MemToReg, MemWrite, mips_alu_1_p3, nand_1_out, OF, RegDest,
       registerfile_1_p4, RegWrite, Tick, ZF;
  wire [1:0] ALUop;
  wire [4:0] Reg_A, Reg_B;
  wire [15:0] Instruction;
  wire [23:0] bit_extender_2_out;
  wire [31:0] adder_1_p3, adder_2_p3, bit_extender_1_out, bit_extender_3_out, Data, mips_alu_1_p2,
       mips_ram_1_p6, mips_ram_1_p7, multiplexer_1_out, PC_q, Result, shifter_1_out;
  wire [31:26] Control_p2;

  Clock clock_1 (.out(Tick));
  Register #(.width(32)) PC (.D(multiplexer_1_out), .Q(PC_q), .clk(Tick));  // open: en, clr
  Register #(.width(6)) OpCode (.D(Control_p2), .clk(Tick));  // open: en, Q, clr
  Multiplexer #(.width(32), .enable("false")) multiplexer_1 (
    .in0(adder_2_p3), .in1(adder_1_p3), .out(multiplexer_1_out), .sel(nand_1_out));
  nand nand_1 (nand_1_out, Branch, ZF);
  // Adder adder_1: pin names not known; wires that end beside it: PC_q, 32'h4, adder_1_p3
  // PLA Control: pin names not known; wires that end beside it: PC_q, Control_p2, {ALUop, ALUsrc, MemWrite, MemRead, MemToReg, RegDest, RegWrite, Branch, Jump}
  assign bit_extender_1_out = {{16{Instruction[15]}}, Instruction};  // Bit_Extender bit_extender_1
  // MIPSProgramROM mipsprogramrom_1: pin names not known; wires that end beside it: {Control_p2, Reg_A, Reg_B, Instruction[4:0], Instruction[9:5], Instruction[15:10]}
  Shifter #(.width(32)) shifter_1 (.in(bit_extender_1_out), .\dist (5'b00010), .out(shifter_1_out));
  // Adder adder_2: pin names not known; wires that end beside it: adder_1_p3, shifter_1_out, adder_2_p3
  Bit_Extender #(.in_width(32), .out_width(24)) bit_extender_2 (.in(Result), .out(bit_extender_2_out));
  // MIPS_RAM mips_ram_1: pin names not known; wires that end beside it: bit_extender_2_out, Data, MemWrite, MemRead, Tick, mips_ram_1_p6, mips_ram_1_p7, Tick
  Multiplexer #(.width(32), .enable("false")) multiplexer_2 (
    .in0(mips_ram_1_p6), .in1(Result), .out(mips_ram_1_p7), .sel(MemToReg));
  // RegisterFile registerfile_1: pin names not known; wires that end beside it: RegWrite, Reg_A, Reg_B, registerfile_1_p4, Data
  // MIPS_ALU mips_alu_1: pin names not known; wires that end beside it: registerfile_1_p4, mips_alu_1_p2, mips_alu_1_p3, mips_alu_1_p3, ZF, Result, OF, ALUop
  Multiplexer #(.width(32), .enable("false")) multiplexer_3 (
    .in0(Data), .in1(bit_extender_3_out), .out(mips_alu_1_p2), .sel(ALUsrc));
  assign bit_extender_3_out = {{16{Instruction[15]}}, Instruction};  // Bit_Extender bit_extender_3
endmodule
